// Logisim project mu0_processor.circ as structural Verilog: 1 circuit, main circuit main
module main (
  input  [15:0] in_1,
  input  [8:0] in_2,
  input  [15:0] in_3,
  input  in_4,
  input  in_5,
  input  IR,
  input  in_7,
  input  in_8,
  input  in_9,
  input  in_10,
  input  R_W_prime,
  input  R_W_prime_2,
  input  in_13,
  input  in_14,
  input  in_15,
  input  [15:0] in_16,
  input  in_17,
  input  [15:0] in_18,
  input  [8:0] in_19
);

  wire clock_1_out, clock_2_out, decoder_1_out0, decoder_1_out1, decoder_1_out2, decoder_1_out3,
       decoder_1_out4, decoder_1_out5, decoder_1_out6, decoder_1_out7, not_1_out, not_2_out;
  wire [3:0] ram_2_data, register_3_q;
  wire [8:0] adder_1_out, multiplexer_1_out, register_1_q, register_2_q;
  wire [11:0] register_3_q_2;
  wire [15:0] adder_2_out, adder_3_out, and_1_out, divider_1_out, multiplexer_2_out, multiplexer_3_out,
       multiplexer_4_out, multiplexer_5_out, multiplier_1_cout, multiplier_1_out, not_3_out, or_1_out,
       ram_1_data, register_4_q, register_5_q, register_6_q, register_7_q, register_8_q, register_9_q,
       register_10_q, register_11_q, register_12_q, register_13_q, shifter_1_out, shifter_2_out,
       shifter_3_out, shifter_4_out, subtractor_1_out, subtractor_2_out;
  wire [15:4] ram_2_data_2;

  Multiplexer #(.width(9), .enable("false")) multiplexer_1 (
    .in0(in_2), .in1(register_1_q), .out(multiplexer_1_out), .sel(in_8));
  Register #(.width(9)) register_1 (.D(adder_1_out), .en(in_17), .Q(register_1_q), .clk(clock_1_out));  // open: clr
  Register #(.width(9)) register_2 (.D(adder_1_out), .en(in_17), .Q(register_2_q), .clk(clock_1_out));  // open: clr
  not not_1 (not_1_out, R_W_prime);
  Adder #(.width(9)) adder_1 (.a(register_2_q), .b(in_19), .out(adder_1_out));  // open: cin, cout
  RAM #(.addrWidth(9), .dataWidth(16), .bus("separate")) ram_1 (
    .addr(multiplexer_1_out), .din(in_18), .data(ram_1_data), .str(R_W_prime), .sel(in_9), .clk(clock_1_out),
    .ld(not_1_out));  // open: clr
  Register #(.width(16)) register_3 (
    .D(ram_1_data), .en(in_17), .Q({register_3_q, register_3_q_2}), .clk(clock_1_out));  // open: clr
  Clock clock_1 (.out(clock_1_out));
  Multiplexer #(.width(16)) multiplexer_2 (
    .in0(in_3), .in1(register_13_q), .out(multiplexer_2_out), .sel(IR), .en(in_5));
  RAM #(.addrWidth(9), .dataWidth(16), .bus("separate")) ram_2 (
    .addr(register_3_q_2[8:0]), .din(multiplexer_2_out), .data({ram_2_data_2, ram_2_data}),
    .str(R_W_prime_2), .sel(in_10), .clk(clock_1_out), .ld(not_2_out));  // open: clr
  not not_2 (not_2_out, R_W_prime_2);
  Multiplexer #(.width(16)) multiplexer_3 (
    .in0(in_1), .in1(register_13_q), .out(multiplexer_3_out), .sel(in_7), .en(in_4));
  Decoder #(.select(3)) decoder_1 (
    .out0(decoder_1_out0), .out1(decoder_1_out1), .out2(decoder_1_out2), .out3(decoder_1_out3),
    .out4(decoder_1_out4), .out5(decoder_1_out5), .out6(decoder_1_out6), .out7(decoder_1_out7),
    .sel(register_3_q_2[11:9]), .en(in_13));
  Register #(.width(16)) register_4 (
    .D(multiplexer_3_out), .en(decoder_1_out0), .Q(register_4_q), .clk(clock_1_out));  // open: clr
  Register #(.width(16)) register_5 (
    .D(multiplexer_3_out), .en(decoder_1_out1), .Q(register_5_q), .clk(clock_1_out));  // open: clr
  Register #(.width(16)) register_6 (
    .D(multiplexer_3_out), .en(decoder_1_out2), .Q(register_6_q), .clk(clock_1_out));  // open: clr
  Register #(.width(16)) register_7 (
    .D(multiplexer_3_out), .en(decoder_1_out3), .Q(register_7_q), .clk(clock_1_out));  // open: clr
  Register #(.width(16)) register_8 (
    .D(multiplexer_3_out), .en(decoder_1_out4), .Q(register_8_q), .clk(clock_1_out));  // open: clr
  Register #(.width(16)) register_9 (
    .D(multiplexer_3_out), .en(decoder_1_out5), .Q(register_9_q), .clk(clock_1_out));  // open: clr
  Register #(.width(16)) register_10 (
    .D(multiplexer_3_out), .en(decoder_1_out6), .Q(register_10_q), .clk(clock_1_out));  // open: clr
  Register #(.width(16)) register_11 (
    .D(multiplexer_3_out), .en(decoder_1_out7), .Q(register_11_q), .clk(clock_1_out));  // open: clr
  Multiplexer #(.select(3), .width(16)) multiplexer_4 (
    .in0(register_4_q), .in1(register_5_q), .in2(register_6_q), .in3(register_7_q), .in4(register_8_q),
    .in5(register_9_q), .in6(register_10_q), .in7(register_11_q), .out(multiplexer_4_out),
    .sel(register_3_q_2[11:9]), .en(in_15));
  Adder #(.width(16)) adder_2 (
    .a(multiplexer_4_out), .b({ram_2_data_2, ram_2_data}), .out(adder_2_out));  // open: cin, cout
  Subtractor #(.width(16)) subtractor_1 (
    .a(multiplexer_4_out), .b({ram_2_data_2, ram_2_data}), .out(subtractor_1_out));  // open: bin, bout
  Multiplier #(.width(16)) multiplier_1 (
    .a(multiplexer_4_out), .b({ram_2_data_2, ram_2_data}), .out(multiplier_1_out), .cout(multiplier_1_cout));  // open: cin
  Divider #(.width(16)) divider_1 (
    .a(multiplexer_4_out), .b({ram_2_data_2, ram_2_data}), .out(divider_1_out));  // open: upper, rem
  Adder #(.width(16)) adder_3 (.a(multiplexer_4_out), .b(in_16), .out(adder_3_out));  // open: cin, cout
  Subtractor #(.width(16)) subtractor_2 (.a(multiplexer_4_out), .b(in_16), .out(subtractor_2_out));  // open: bin, bout
  assign and_1_out = multiplexer_4_out & {ram_2_data_2, ram_2_data};  // AND_Gate and_1, 16 bits wide
  assign or_1_out = multiplexer_4_out | multiplexer_4_out;  // OR_Gate or_1, 16 bits wide
  assign not_3_out = ~multiplexer_4_out;  // NOT_Gate not_3, 16 bits wide
  Register #(.width(16)) register_12 (
    .D({ram_2_data_2, ram_2_data}), .Q(register_12_q), .clk(clock_1_out));  // open: en, clr
  Shifter #(.width(16), .shift("lr")) shifter_1 (.in(multiplexer_4_out), .\dist (ram_2_data), .out(shifter_1_out));
  Shifter #(.width(16)) shifter_2 (.in(multiplexer_4_out), .\dist (ram_2_data), .out(shifter_2_out));
  Shifter #(.width(16), .shift("rr")) shifter_3 (.in(multiplexer_4_out), .\dist (ram_2_data), .out(shifter_3_out));
  Shifter #(.width(16), .shift("rl")) shifter_4 (.in(multiplexer_4_out), .\dist (ram_2_data), .out(shifter_4_out));
  Multiplexer #(.select(4), .width(16), .enable("false")) multiplexer_5 (
    .in0({ram_2_data_2, ram_2_data}), .in1(multiplexer_4_out), .in2(adder_2_out), .in3(subtractor_1_out),
    .in4(multiplier_1_out), .in5(divider_1_out), .in6(adder_3_out), .in7(subtractor_2_out), .in8(and_1_out),
    .in9(or_1_out), .in10(not_3_out), .in11(register_12_q), .in12(shifter_1_out), .in13(shifter_2_out),
    .in14(shifter_3_out), .in15(shifter_4_out), .out(multiplexer_5_out), .sel(register_3_q));
  Register #(.width(16)) register_13 (
    .D(multiplexer_5_out), .en(in_14), .Q(register_13_q), .clk(clock_2_out));  // open: clr
  Clock clock_2 (.out(clock_2_out));

  // Notes on the sheet:
  //   MAR
  //   PC
  //   WORD SIZE
  //   CODE MEMORY
  //   INPUT TO DATA MEMORY
  //   INSTRUCTION TO BE GIVEN
  //   mu0 Processor 
  //   DATA MEMORY
  //   INPUT TO REGISTERS
  //   R0
  //   R1
  //   R2
  //   R3
  //   R4
  //   R5
  //   R6
  //   R7
  //   INCREAMENT
  //   BY
  //   OUTPUT
endmodule
